// Logisim project parte_b.circ as structural Verilog: 5 circuits, main circuit latch_rs
module latch_rs (
  input  in_1,
  input  in_2,
  output out_3,
  output out_4
);

  nor nor_1 (out_3, in_2, out_4);
  nor nor_2 (out_4, out_3, in_1);
endmodule

module latch_jk (
  input  in_1,
  input  in_2,
  output out_3,
  output out_4
);

  wire and_1_out, and_2_out;

  and and_1 (and_1_out, out_4, in_1);
  and and_2 (and_2_out, in_2, out_3);
  nor nor_1 (out_3, and_2_out, out_4);
  nor nor_2 (out_4, out_3, and_1_out);
endmodule

module latch_d (
  input  in_1,
  input  in_2,
  output out_3,
  output out_4
);

  wire and_1_out, and_2_out, not_1_out;

  not not_1 (not_1_out, in_1);
  and and_1 (and_1_out, in_1, in_2);
  and and_2 (and_2_out, in_2, not_1_out);
  nor nor_1 (out_3, and_2_out, out_4);
  nor nor_2 (out_4, out_3, and_1_out);
endmodule

module ej_4_registro_simple (
  input  in_1,
  input  in_2,
  input  in_3,
  input  in_4,
  input  in_5,
  output out_6,
  output out_7,
  output out_8,
  output out_9
);

  wire and_1_out, clock_1_out;

  Clock clock_1 (.out(clock_1_out));
  Register #(.width(1)) register_1 (.D(in_1), .Q(out_6), .clk(and_1_out));  // open: en, clr
  and and_1 (and_1_out, clock_1_out, in_5);
  Register #(.width(1)) register_2 (.D(in_2), .Q(out_7), .clk(and_1_out));  // open: en, clr
  Register #(.width(1)) register_3 (.D(in_3), .Q(out_8), .clk(and_1_out));  // open: en, clr
  Register #(.width(1)) register_4 (.D(in_4), .Q(out_9), .clk(and_1_out));  // open: en, clr
endmodule

module ej_5_registro_bidireccional (
  input  in_1,
  input  in_2,
  input  in_3,
  input  in_4,
  input  in_5,
  input  in_6
);

  wire and_1_out, clock_1_out, controlled_buffer_1_out, controlled_buffer_3_out, controlled_buffer_5_out,
       register_1_q, register_2_q, register_3_q, register_4_q;

  assign controlled_buffer_1_out = in_5 ? in_1 : 1'bz;  // Controlled_Buffer controlled_buffer_1
  Clock clock_1 (.out(clock_1_out));
  Controlled_Buffer controlled_buffer_2 (.in(register_1_q), .en(in_5));  // open: out
  Register #(.width(1)) register_1 (.D(controlled_buffer_1_out), .Q(register_1_q), .clk(and_1_out));  // open: en, clr
  and and_1 (and_1_out, clock_1_out, in_6);
  assign controlled_buffer_3_out = in_5 ? register_2_q : 1'bz;  // Controlled_Buffer controlled_buffer_3
  Register #(.width(1)) register_2 (.D(in_2), .Q(register_2_q), .clk(and_1_out));  // open: en, clr
  assign in_3 = in_5 ? register_3_q : 1'bz;  // Controlled_Buffer controlled_buffer_4
  Register #(.width(1)) register_3 (.D(in_3), .Q(register_3_q), .clk(and_1_out));  // open: en, clr
  assign controlled_buffer_5_out = in_5 ? register_4_q : 1'bz;  // Controlled_Buffer controlled_buffer_5
  Register #(.width(1)) register_4 (.D(in_4), .Q(register_4_q), .clk(and_1_out));  // open: en, clr
endmodule
